# Fritzing sketch led_transistor (saved by Fritzing 0.9.3b)
circuit board: 3.96592cm x 3.41981cm
breadboards: 1

parts:
  Q7 = TRANSISTOR_NPN [package=to-92-ammo]
  Q8 = TRANSISTOR_NPN [package=to-92-ammo]
  Q9 = TRANSISTOR_NPN [package=to-92-ammo]
  Q10 = PNP-Transistor [package="TO92 [THT]"]
  R1 = Resistor [tolerance=±5% resistance=220 package=THT]
  R2 = Resistor [tolerance=±5% resistance=220 package=THT]
  R3 = Resistor [tolerance=±5% resistance=220 package=THT]
  J1 = female pin header, 4 pins [form="♀ (female)"]
  R4 = Resistor [tolerance=±5% resistance=220 package=THT]
  J2 = female pin header, 2 pins [form="♀ (female)"]
  J3 = female pin header, 2 pins [form="♀ (female)"]
  J4 = female pin header, 4 pins [form="♀ (female)"]

nets:
  N1: Q7.E, R3.Pin_0
  N2: Q7.B, J1.pin4
  N3: Q7.C, Q8.C, Q9.C, Q10.E, J2.pin1
  N4: Q8.E, R1.Pin_0
  N5: Q8.B, J1.pin2
  N6: Q9.E, R2.Pin_0
  N7: Q9.B, J1.pin3
  N8: Q10.B, J1.pin1
  N9: Q10.C, R4.Pin_0
  N10: R1.Pin_1, J4.pin2
  N11: R2.Pin_1, J4.pin3
  N12: R3.Pin_1, J4.pin4
  N13: R4.Pin_1, J3.pin2
  N14: J2.pin2, J3.pin1, J4.pin1
