# Fritzing sketch new_mb_v3 (saved by Fritzing 0.9.3b)
circuit board: 10cm x 5.1cm
breadboards: 1

parts:
  Teensy_3_1 = Teensy 3.1
  gy-88 = rounded female pin header, 8 pins [form="♀ (female rounded)"]
  -_fan_+ = female pin header, 2 pins [form="♀ (female)"]
  R1 = Resistor [tolerance=±5% resistance=4.7k package=THT]
  R2 = Resistor [tolerance=±5% resistance=10k package=THT]
  Serial = female pin header, 4 pins [form="♀ (female)"]
  +_7_4v_out_- = female pin header, 2 pins [form="♀ (female)"]
  -_7_4vin_+1 = female pin header, 3 pins [form="♀ (female)"]
  -_5v_in_+ = female pin header, 2 pins [form="♀ (female)"]
  i2c_2 = female pin header, 2 pins [form="♀ (female)"]
  +_5v_out_- = female pin header, 2 pins [form="♀ (female)"]
  -_5v_out_+ = female pin header, 2 pins [form="♀ (female)"]
  DS2 = DS18B20 1-Wire Temperature Sensor [part_number=DS18B20]
  motorCtrl4 = female pin header, 2 pins [form="♀ (female)"]
  J7 = female pin header, 1 pin [form="♀ (female)"]
  J8 = female pin header, 1 pin [form="♀ (female)"]
  J9 = female pin header, 1 pin [form="♀ (female)"]
  J10 = female pin header, 1 pin [form="♀ (female)"]
  J11 = female pin header, 1 pin [form="♀ (female)"]
  J12 = female pin header, 1 pin [form="♀ (female)"]
  J13 = female pin header, 1 pin [form="♀ (female)"]
  J14 = female pin header, 1 pin [form="♀ (female)"]
  serial2 = female pin header, 2 pins [form="♀ (female)"]
  serial3 = female pin header, 2 pins [form="♀ (female)"]
  5v_out4 = female pin header, 2 pins [form="♀ (female)"]
  MP6500 = DRV 8825 Stepper Motor Carrier, High Current [part_number="DRV 8825"]
  A2_A1_B1_B2 = female pin header, 4 pins [form="♀ (female)"]
  stepper1 = female pin header, 4 pins [form="♀ (female)"]
  steps = female pin header, 4 pins [form="♀ (female)"]
  +_-_SCL_SDA = female pin header, 4 pins [form="♀ (female)"]
  a_sens = female pin header, 3 pins [form="♀ (female)"]
  S8050 = TRANSISTOR_NPN [package=to-92-ammo]
  5v_|_7_4v = female pin header, 3 pins [form="♀ (female)"]
  C1 = Ceramic Capacitor [capacitance=1pF package="100 mil [THT, multilayer]"]
  D1 = Diode [package=diode-1n4001]
  5v_|_7_4v_2 = female pin header, 3 pins [form="♀ (female)"]
  L293D = L293D [package=THT]
  L293D_2 = L293D [package=THT]
  +_7_4v_out_-_2 = female pin header, 2 pins [form="♀ (female)"]
  endstop = female pin header, 2 pins [form="♀ (female)"]
  R3 = Resistor [tolerance=±5% resistance=4.7k package=THT]
  7v|5v = female pin header, 3 pins [form="♀ (female)"]
  a_sens1 = female pin header, 1 pin [form="♀ (female)"]
  C2 = Capacitor Polarized [package=cpol-radial-10uf-25v]
  C3 = Ceramic Capacitor [capacitance=100nF package="200 mil [THT, multilayer]"]
  C6 = Capacitor [package=cap-pth-small]
  C9 = Capacitor [package=cap-pth-small]
  C10 = Capacitor [package=cap-pth-small]
  Stepper_Logic_Supply = female pin header, 2 pins [form="♀ (female)"]
  C11 = Ceramic Capacitor [capacitance=100nF package="200 mil [THT, multilayer]"]

nets:
  GND: Teensy_3_1.GND, gy-88.pin6, R2.Pin_1, Serial.pin4, +_7_4v_out_-.pin1, -_7_4vin_+1.pin3, -_5v_in_+.pin2, +_5v_out_-.pin1, -_5v_out_+.pin2, DS2.GND, 5v_out4.pin1, MP6500.VOLTAGE_ST/_MT, MP6500.GROUND_ST/_MT, MP6500.GROUND_LOG, +_-_SCL_SDA.pin3, S8050.C, 5v_|_7_4v.pin1, 5v_|_7_4v_2.pin2, L293D.0V, L293D_2.0V, +_7_4v_out_-_2.pin1, C2.-, C3.0, C6.2, C9.1, C9.2, C10.1, C11.0, C11.1
  N1: Teensy_3_1.D0, Serial.pin3
  N2: Teensy_3_1.D1, Serial.pin2
  N3: Teensy_3_1.D2, R1.Pin_1, DS2.DQ, C10.2
  N4: Teensy_3_1.D3, L293D_2.Enable_1, L293D_2.Enable_2
  N5: Teensy_3_1.D4, L293D.Enable_1, L293D.Enable_2
  N6: Teensy_3_1.D5, L293D_2.In_1, L293D_2.In_4
  N7: Teensy_3_1.D6, L293D_2.In_2, L293D_2.In_3
  N8: Teensy_3_1.D7, serial3.pin2
  N9: Teensy_3_1.D8, serial3.pin1
  N10: Teensy_3_1.D9, serial2.pin2
  N11: Teensy_3_1.D10, serial2.pin1
  N12: Teensy_3_1.D11, L293D.In_1, L293D.In_4
  N13: Teensy_3_1.D12, L293D.In_2, L293D.In_3
  N14: Teensy_3_1.D13, R2.Pin_0, endstop.pin1
  N15: Teensy_3_1.A1/D15, MP6500.SLEEP
  N16: Teensy_3_1.A2/D16, MP6500.DIRECTION
  N17: Teensy_3_1.A4/D18, gy-88.pin4, +_-_SCL_SDA.pin1
  N18: Teensy_3_1.A5/D19, gy-88.pin5, +_-_SCL_SDA.pin2
  N19: Teensy_3_1.A6/D20, MP6500.STEP
  N20: Teensy_3_1.A7/D21, R3.Pin_1
  N21: Teensy_3_1.A9/D23, a_sens.pin1
  N22: Teensy_3_1.3V3, gy-88.pin7, +_-_SCL_SDA.pin4, a_sens.pin2, endstop.pin2
  N23: Teensy_3_1.AGND, a_sens.pin3
  VIN: Teensy_3_1.Vin, R1.Pin_0, Serial.pin1, -_5v_in_+.pin1, +_5v_out_-.pin2, -_5v_out_+.pin1, DS2.VDD, 5v_out4.pin2, steps.pin1, steps.pin2, steps.pin3, steps.pin4, 5v_|_7_4v.pin3, 5v_|_7_4v_2.pin3, L293D.+V, L293D_2.+V, 7v|5v.pin1, a_sens1.pin1, C2.+, C3.1, C6.1, Stepper_Logic_Supply.pin1
  N24: -_fan_+.pin1, 5v_|_7_4v.pin2, C1.1, D1.C
  N25: -_fan_+.pin2, S8050.E, C1.0, D1.A
  N26: +_7_4v_out_-.pin2, -_7_4vin_+1.pin1, 5v_|_7_4v_2.pin1, +_7_4v_out_-_2.pin2, 7v|5v.pin3
  N27: i2c_2.pin1, motorCtrl4.pin1
  N28: i2c_2.pin2, motorCtrl4.pin2
  N29: J7.pin1, L293D_2.Out_1_(_Controlled_by_Enable_1_)
  N30: J8.pin1, L293D.Out_2_(_Controlled_by_Enable_1_)
  N31: J9.pin1, L293D_2.Out_2_(_Controlled_by_Enable_1_)
  N32: J10.pin1, L293D.Out_1_(_Controlled_by_Enable_1_)
  N33: J11.pin1, L293D_2.Out_3_(_Controlled_by_Enable_2_)
  N34: J12.pin1, L293D_2.Out_4_(_Controlled_by_Enable_2_)
  N35: J13.pin1, L293D.Out_4_(_Controlled_by_Enable_2_)
  N36: J14.pin1, L293D.Out_3_(_Controlled_by_Enable_2_)
  N37: MP6500.MS1, stepper1.pin4
  N38: MP6500.MS2, stepper1.pin3
  N39: MP6500.MS3, stepper1.pin2
  N40: MP6500.RESET, stepper1.pin1
  N41: MP6500.OUT_2B, A2_A1_B1_B2.pin1
  N42: MP6500.OUT_2A, A2_A1_B1_B2.pin2
  N43: MP6500.OUT_1A, A2_A1_B1_B2.pin3
  N44: MP6500.OUT_1B, A2_A1_B1_B2.pin4
  N45: MP6500.VOLTAGE_DD, Stepper_Logic_Supply.pin2
  N46: S8050.B, R3.Pin_0
  N47: L293D.+Vmotor, L293D_2.+Vmotor, 7v|5v.pin2

notes:
  ζ2 Motherboard
