# Fritzing sketch smd_motherboard_v2 (saved by Fritzing 0.9.3b)
circuit board: 6.50445cm x 3.0101cm
breadboards: 1

parts:
  L293DD = L293DD [package=SO(w)]
  L293DD1 = L293DD [package=SO(w)]
  ULN2003A = ULN2003A [package="SO16 [SMD]"]  # not connected
  USB = USB Connectors [package=usb-microb]
  HMC5883L = HMC5883L [package=16lpcc]
  BMP085 = BMP085 Pressure Sensor [package=bmp085]
  R1 = Resistor [tolerance=±5% resistance=1k package="0603 [SMD]"]  # not connected
  R2 = Resistor [tolerance=±5% resistance=1k package="0603 [SMD]"]  # not connected
  2n2222 = PNP-Transistor [package="SOT-23 [SMD]"]
  2n2222_2 = PNP-Transistor [package="SOT-23 [SMD]"]
  C2 = Ceramic Capacitor [capacitance="100 nF" package="0603 [SMD, multilayer]"]
  C3 = Ceramic Capacitor [capacitance=10pF voltage=6.3V package="0603 [SMD, multilayer]"]  # not connected
  C4 = Ceramic Capacitor [capacitance=10pF voltage=6.3V package="0603 [SMD, multilayer]"]  # not connected
  R3 = Resistor [tolerance=±5% resistance=4.7k package="0603 [SMD]"]
  R4 = Resistor [tolerance=±5% resistance=10k package="0603 [SMD]"]
  R5 = Resistor [tolerance=±5% resistance=33 package="0603 [SMD]"]  # not connected
  R6 = Resistor [tolerance=±5% resistance=33 package="0603 [SMD]"]  # not connected
  F1 = Resettable Fuse PTC [package=0603]  # not connected
  IC1 = USB UART [package=ssop28db]
  IRF7401 = SO08 [chip_label=SO08 package=SO]  # not connected
  MCP_1700-3302 = LM3480IM4 [package=sot23-3]
  MPU6050 = QFN-24 [chip_label=SO16 package=QFN]
  C5 = Ceramic Capacitor [capacitance=1µF voltage=6.3V package="0603 [SMD, multilayer]"]
  C6 = Ceramic Capacitor [capacitance=2.2nF voltage=6.3V package="0603 [SMD, multilayer]"]
  C7 = Ceramic Capacitor [capacitance=0.01µF voltage=6.3V package="0603 [SMD, multilayer]"]
  C8 = Ceramic Capacitor [capacitance=0.1µF voltage=6.3V package="0603 [SMD, multilayer]"]
  C9 = Ceramic Capacitor [capacitance=0.22µF voltage=6.3V package="0603 [SMD, multilayer]"]
  C10 = Ceramic Capacitor [capacitance=4.7µF voltage=6.3V package="0603 [SMD, multilayer]"]
  C11 = Ceramic Capacitor [capacitance=0.1µF voltage=6.3V package="0603 [SMD, multilayer]"]
  C12 = Ceramic Capacitor [capacitance=04.7µF voltage=6.3V package="0603 [SMD, multilayer]"]
  C13 = Ceramic Capacitor [capacitance=10µF voltage=6.3V package="0603 [SMD, multilayer]"]
  C14 = Ceramic Capacitor [capacitance=0.1µF voltage=6.3V package="0603 [SMD, multilayer]"]
  C15 = Ceramic Capacitor [capacitance=0.1µF voltage=6.3V package="0603 [SMD, multilayer]"]
  Bauteil1 = SO08 [chip_label=SO16 package=SO]  # not connected
  IC2 = SN74LVC2G14DBVR [package=SOT23-6]  # not connected
  STM32F103CBT6 = STM32F103 [package=LQFP-48]
  MP6500GU = QFN-24 [chip_label=SO16 package=QFN]
  C16 = Ceramic Capacitor [capacitance=100nF voltage=6.3V package="0603 [SMD, multilayer]"]
  R7 = Resistor [tolerance=±5% resistance=220k package="0603 [SMD]"]
  C17 = Ceramic Capacitor [capacitance=0.22µF voltage=6.3V package="0603 [SMD, multilayer]"]
  C18 = Ceramic Capacitor [capacitance=1µF voltage=6.3V package="0603 [SMD, multilayer]"]
  Stepper_Motor = Header 4 [package=jst-4-pth]
  U2 = V_REG_MIC2920 [package=sot223]  # not connected
  SN754410 = STM32F103 [package=LQFP-48]  # not connected
  LM1084 = Voltage Regulator [package=to-220-alt]  # not connected
  7_4v_in = Header 2 [package=jst-2-pth]
  MCP_1700-3303 = LM3480IM4 [package=sot23-3]  # not connected

nets:
  N1: L293DD.Input_1#1, L293DD.Input_2#18, 2n2222.2
  GND: L293DD.GND, L293DD1.GND, 2n2222.1, 2n2222_2.1
  N2: L293DD.Input_1#8, L293DD.Input_2#11, 2n2222.0
  N3: L293DD.Vs, L293DD1.Vs
  VSS: L293DD.Vss, L293DD1.Vss
  N4: L293DD1.Input_1#1, L293DD1.Input_2#18, 2n2222_2.0
  N5: L293DD1.Input_1#8, L293DD1.Input_2#11, 2n2222_2.2
  N6: USB.D+, IC1.USBDP
  N7: USB.D-, IC1.USBDM
  N8: HMC5883L.SCL, BMP085.SCL, MPU6050.SCL
  VDD: HMC5883L.VDD, HMC5883L.S1, HMC5883L.VDDIO, BMP085.VDDA, BMP085.VDDD, MCP_1700-3302.OUT, MPU6050.VLOGIC, MPU6050.VDD, C5.0, C7.1, C11.1, C13.0, C14.0, C15.0
  N9: HMC5883L.SETP, C9.0
  GND_2: HMC5883L.GND, HMC5883L.C1, BMP085.GND, MCP_1700-3302.GND, MPU6050.CLKIN, MPU6050.GND, C5.1, C6.1, C7.0, C10.0, C10.1, C11.0, C12.1, C13.1, C14.1, C15.1, MP6500GU.AGND, MP6500GU.GND, R7.Pin_0, C17.0, 7_4v_in.1
  N10: HMC5883L.SETC, C9.1
  N11: HMC5883L.SDA, BMP085.SDA, MPU6050.SDA
  N12: C2.1, IC1.RESET
  N13: R3.Pin_1, R4.Pin_0
  GND_3: IC1.GND7, IC1.GND18, IC1.GND21, IC1.AGND, IC1.TEST
  5V: IC1.VCC
  N14: MCP_1700-3302.IN, C12.0, 7_4v_in.2
  N15: MPU6050.REGOUT, C8.0
  N16: MPU6050.FSYNC, C8.1
  N17: MPU6050.CPOUT, C6.0
  N18: STM32F103CBT6.VSS_1, STM32F103CBT6.VSS_2
  N19: MP6500GU.ROSC, R7.Pin_1
  N20: MP6500GU.BOUT1, Stepper_Motor.2
  N21: MP6500GU.VIN, C18.0
  N22: MP6500GU.BOUT2, Stepper_Motor.1
  N23: MP6500GU.VCP, C18.1
  N24: MP6500GU.CP2, C16.1
  N25: MP6500GU.CP1, C16.0
  N26: MP6500GU.VG, C17.1
  N27: MP6500GU.AOUT2, Stepper_Motor.4
  N28: MP6500GU.AOUT1, Stepper_Motor.3
